// Digital circuit BancoDeRegistradores.dig as structural Verilog
module BancoDeRegistradores (
  input  [3:0] a,
  input  [3:0] b,
  input  [3:0] c,
  input  [31:0] C_2,
  input  clk,
  input  W_E,
  output [31:0] A_2,
  output [31:0] B_2
);

  wire demultiplexer_1_out_0, demultiplexer_1_out_1, demultiplexer_1_out_2, demultiplexer_1_out_3,
       demultiplexer_1_out_4, demultiplexer_1_out_5, demultiplexer_1_out_6, demultiplexer_1_out_7,
       demultiplexer_1_out_8, demultiplexer_1_out_9, demultiplexer_1_out_10, demultiplexer_1_out_11,
       demultiplexer_1_out_12, demultiplexer_1_out_13, demultiplexer_1_out_14, demultiplexer_1_out_15;
  wire [31:0] d_ff_1_q, d_ff_2_q, d_ff_3_q, d_ff_4_q, d_ff_5_q, d_ff_6_q, d_ff_7_q, d_ff_8_q, d_ff_9_q,
       d_ff_10_q, d_ff_11_q, d_ff_12_q, d_ff_13_q, d_ff_14_q, d_ff_15_q, d_ff_16_q, multiplexer_1_out,
       multiplexer_2_out, multiplexer_3_out, multiplexer_4_out, multiplexer_5_out, multiplexer_6_out,
       multiplexer_7_out, multiplexer_8_out, multiplexer_9_out, multiplexer_10_out, multiplexer_11_out,
       multiplexer_12_out, multiplexer_13_out, multiplexer_14_out, multiplexer_15_out, multiplexer_16_out;

  Demultiplexer #(.Selector_Bits(4)) demultiplexer_1 (
    .sel(c), .in(W_E), .out_0(demultiplexer_1_out_0), .out_1(demultiplexer_1_out_1),
    .out_2(demultiplexer_1_out_2), .out_3(demultiplexer_1_out_3), .out_4(demultiplexer_1_out_4),
    .out_5(demultiplexer_1_out_5), .out_6(demultiplexer_1_out_6), .out_7(demultiplexer_1_out_7),
    .out_8(demultiplexer_1_out_8), .out_9(demultiplexer_1_out_9), .out_10(demultiplexer_1_out_10),
    .out_11(demultiplexer_1_out_11), .out_12(demultiplexer_1_out_12), .out_13(demultiplexer_1_out_13),
    .out_14(demultiplexer_1_out_14), .out_15(demultiplexer_1_out_15));
  Multiplexer #(.Bits(32)) multiplexer_1 (
    .sel(demultiplexer_1_out_0), .in_0(d_ff_1_q), .in_1(d_ff_1_q), .out(multiplexer_1_out));
  D_FF #(.Bits(32)) d_ff_1 (.D(multiplexer_1_out), .C(clk), .Q(d_ff_1_q));  // open: nQ
  Multiplexer #(.Bits(32)) multiplexer_2 (
    .sel(demultiplexer_1_out_1), .in_0(d_ff_2_q), .in_1(C_2), .out(multiplexer_2_out));
  D_FF #(.Bits(32)) d_ff_2 (.D(multiplexer_2_out), .C(clk), .Q(d_ff_2_q));  // open: nQ
  Multiplexer #(.Bits(32)) multiplexer_3 (
    .sel(demultiplexer_1_out_2), .in_0(d_ff_3_q), .in_1(C_2), .out(multiplexer_3_out));
  D_FF #(.Bits(32)) d_ff_3 (.D(multiplexer_3_out), .C(clk), .Q(d_ff_3_q));  // open: nQ
  Multiplexer #(.Bits(32)) multiplexer_4 (
    .sel(demultiplexer_1_out_3), .in_0(d_ff_4_q), .in_1(C_2), .out(multiplexer_4_out));
  D_FF #(.Bits(32)) d_ff_4 (.D(multiplexer_4_out), .C(clk), .Q(d_ff_4_q));  // open: nQ
  Multiplexer #(.Bits(32)) multiplexer_5 (
    .sel(demultiplexer_1_out_4), .in_0(d_ff_5_q), .in_1(C_2), .out(multiplexer_5_out));
  D_FF #(.Bits(32)) d_ff_5 (.D(multiplexer_5_out), .C(clk), .Q(d_ff_5_q));  // open: nQ
  Multiplexer #(.Bits(32)) multiplexer_6 (
    .sel(demultiplexer_1_out_5), .in_0(d_ff_6_q), .in_1(C_2), .out(multiplexer_6_out));
  D_FF #(.Bits(32)) d_ff_6 (.D(multiplexer_6_out), .C(clk), .Q(d_ff_6_q));  // open: nQ
  Multiplexer #(.Bits(32)) multiplexer_7 (
    .sel(demultiplexer_1_out_6), .in_0(d_ff_7_q), .in_1(C_2), .out(multiplexer_7_out));
  D_FF #(.Bits(32)) d_ff_7 (.D(multiplexer_7_out), .C(clk), .Q(d_ff_7_q));  // open: nQ
  Multiplexer #(.Bits(32)) multiplexer_8 (
    .sel(demultiplexer_1_out_7), .in_0(d_ff_8_q), .in_1(C_2), .out(multiplexer_8_out));
  D_FF #(.Bits(32)) d_ff_8 (.D(multiplexer_8_out), .C(clk), .Q(d_ff_8_q));  // open: nQ
  Multiplexer #(.Bits(32)) multiplexer_9 (
    .sel(demultiplexer_1_out_8), .in_0(d_ff_9_q), .in_1(C_2), .out(multiplexer_9_out));
  D_FF #(.Bits(32)) d_ff_9 (.D(multiplexer_9_out), .C(clk), .Q(d_ff_9_q));  // open: nQ
  Multiplexer #(.Bits(32)) multiplexer_10 (
    .sel(demultiplexer_1_out_9), .in_0(d_ff_10_q), .in_1(C_2), .out(multiplexer_10_out));
  D_FF #(.Bits(32)) d_ff_10 (.D(multiplexer_10_out), .C(clk), .Q(d_ff_10_q));  // open: nQ
  Multiplexer #(.Bits(32)) multiplexer_11 (
    .sel(demultiplexer_1_out_10), .in_0(d_ff_11_q), .in_1(C_2), .out(multiplexer_11_out));
  D_FF #(.Bits(32)) d_ff_11 (.D(multiplexer_11_out), .C(clk), .Q(d_ff_11_q));  // open: nQ
  Multiplexer #(.Bits(32)) multiplexer_12 (
    .sel(demultiplexer_1_out_11), .in_0(d_ff_12_q), .in_1(C_2), .out(multiplexer_12_out));
  D_FF #(.Bits(32)) d_ff_12 (.D(multiplexer_12_out), .C(clk), .Q(d_ff_12_q));  // open: nQ
  Multiplexer #(.Bits(32)) multiplexer_13 (
    .sel(demultiplexer_1_out_12), .in_0(d_ff_13_q), .in_1(C_2), .out(multiplexer_13_out));
  D_FF #(.Bits(32)) d_ff_13 (.D(multiplexer_13_out), .C(clk), .Q(d_ff_13_q));  // open: nQ
  Multiplexer #(.Bits(32)) multiplexer_14 (
    .sel(demultiplexer_1_out_13), .in_0(d_ff_14_q), .in_1(C_2), .out(multiplexer_14_out));
  D_FF #(.Bits(32)) d_ff_14 (.D(multiplexer_14_out), .C(clk), .Q(d_ff_14_q));  // open: nQ
  Multiplexer #(.Bits(32)) multiplexer_15 (
    .sel(demultiplexer_1_out_14), .in_0(d_ff_15_q), .in_1(C_2), .out(multiplexer_15_out));
  D_FF #(.Bits(32)) d_ff_15 (.D(multiplexer_15_out), .C(clk), .Q(d_ff_15_q));  // open: nQ
  Multiplexer #(.Bits(32)) multiplexer_16 (
    .sel(demultiplexer_1_out_15), .in_0(d_ff_16_q), .in_1(C_2), .out(multiplexer_16_out));
  D_FF #(.Bits(32)) d_ff_16 (.D(multiplexer_16_out), .C(clk), .Q(d_ff_16_q));  // open: nQ
  Multiplexer #(.Selector_Bits(4), .Bits(32)) multiplexer_17 (
    .sel(a), .in_0(d_ff_1_q), .in_1(d_ff_2_q), .in_2(d_ff_3_q), .in_3(d_ff_4_q), .in_4(d_ff_5_q),
    .in_5(d_ff_6_q), .in_6(d_ff_7_q), .in_7(d_ff_8_q), .in_8(d_ff_9_q), .in_9(d_ff_10_q), .in_10(d_ff_11_q),
    .in_11(d_ff_12_q), .in_12(d_ff_13_q), .in_13(d_ff_14_q), .in_14(d_ff_15_q), .in_15(d_ff_16_q), .out(A_2));
  Multiplexer #(.Selector_Bits(4), .Bits(32)) multiplexer_18 (
    .sel(b), .in_0(d_ff_1_q), .in_1(d_ff_2_q), .in_2(d_ff_3_q), .in_3(d_ff_4_q), .in_4(d_ff_5_q),
    .in_5(d_ff_6_q), .in_6(d_ff_7_q), .in_7(d_ff_8_q), .in_8(d_ff_9_q), .in_9(d_ff_10_q), .in_10(d_ff_11_q),
    .in_11(d_ff_12_q), .in_12(d_ff_13_q), .in_13(d_ff_14_q), .in_14(d_ff_15_q), .in_15(d_ff_16_q), .out(B_2));
endmodule
