// Digital circuit CarryLookAhead4Bits.dig as structural Verilog
module CarryLookAhead4Bits (
  input  [3:0] A,
  input  [3:0] B,
  input  C_In,
  output S0,
  output S1,
  output S2,
  output S3,
  output C_Out
);

  wire and_1_out, and_2_out, and_3_out, and_4_out, and_5_out, and_6_out, and_7_out, and_8_out, and_9_out,
       and_10_out, gp_1_g, gp_1_p, gp_2_g, gp_2_p, gp_3_g, gp_3_p, gp_4_g, gp_4_p, or_1_out, or_2_out,
       or_3_out;

  GP gp_1 (.A(A[0]), .B(B[0]), .G(gp_1_g), .P(gp_1_p));
  GP gp_2 (.A(A[1]), .B(B[1]), .G(gp_2_g), .P(gp_2_p));
  GP gp_3 (.A(A[2]), .B(B[2]), .G(gp_3_g), .P(gp_3_p));
  GP gp_4 (.A(A[3]), .B(B[3]), .G(gp_4_g), .P(gp_4_p));
  xor xor_1 (S0, C_In, gp_1_p);
  and and_1 (and_1_out, gp_1_p, C_In);
  and and_2 (and_2_out, C_In, gp_2_p, gp_1_p);
  and and_3 (and_3_out, gp_1_g, gp_2_p);
  and and_4 (and_4_out, C_In, gp_1_p, gp_2_p, gp_3_p);
  and and_5 (and_5_out, gp_1_g, gp_2_p, gp_3_p);
  and and_6 (and_6_out, gp_2_g, gp_3_p);
  and and_7 (and_7_out, gp_1_p, gp_2_p, C_In, gp_3_p, gp_4_p);
  and and_8 (and_8_out, gp_1_g, gp_2_p, gp_3_p, gp_4_p);
  and and_9 (and_9_out, gp_2_g, gp_3_p, gp_4_p);
  and and_10 (and_10_out, gp_3_g, gp_4_p);
  or or_1 (or_1_out, and_1_out, gp_1_g);
  or or_2 (or_2_out, and_2_out, gp_2_g, and_3_out);
  or or_3 (or_3_out, and_4_out, and_5_out, and_6_out, gp_3_g);
  xor xor_2 (S1, or_1_out, gp_2_p);
  xor xor_3 (S2, or_2_out, gp_3_p);
  xor xor_4 (S3, gp_4_p, or_3_out);
  or or_4 (C_Out, and_7_out, and_8_out, and_9_out, and_10_out, gp_4_g);
endmodule
