// Digital circuit CarrySelect32Bits.dig as structural Verilog
module CarrySelect32Bits (
  input  [31:0] A,
  input  [31:0] B,
  input  [2:0] \Subtração ,
  output [31:0] S
);

  wire carryselect4bits_1_c_out, carryselect4bits_2_c_out, carryselect4bits_3_c_out,
       carryselect4bits_4_c_out, carryselect4bits_5_c_out, carryselect4bits_6_c_out, fulladder_1_c_out,
       fulladder_2_c_out, fulladder_3_c_out, fulladder_4_c_out;
  wire [3:0] multiplexer_1_out, multiplexer_1_out_2, multiplexer_1_out_3, multiplexer_1_out_4,
       multiplexer_1_out_5, multiplexer_1_out_6, multiplexer_1_out_7, multiplexer_1_out_8;
  wire [31:0] not_1_out;

  Multiplexer #(.Bits(32)) multiplexer_1 (
    .sel(\Subtração [0]), .in_0(B), .in_1(not_1_out),
    .out({multiplexer_1_out_8, multiplexer_1_out_7, multiplexer_1_out_6, multiplexer_1_out_5, multiplexer_1_out_4, multiplexer_1_out_3, multiplexer_1_out_2, multiplexer_1_out}));
  assign not_1_out = ~B;  // Not not_1, 32 bits wide
  FullAdder fulladder_1 (
    .A(A[0]), .B(multiplexer_1_out[0]), .C_In(\Subtração [0]), .S(S[0]), .C_Out(fulladder_1_c_out));
  FullAdder fulladder_2 (
    .A(A[1]), .B(multiplexer_1_out[1]), .C_In(fulladder_1_c_out), .S(S[1]), .C_Out(fulladder_2_c_out));
  FullAdder fulladder_3 (
    .A(A[2]), .B(multiplexer_1_out[2]), .C_In(fulladder_2_c_out), .S(S[2]), .C_Out(fulladder_3_c_out));
  FullAdder fulladder_4 (
    .A(A[3]), .B(multiplexer_1_out[3]), .C_In(fulladder_3_c_out), .S(S[3]), .C_Out(fulladder_4_c_out));
  CarrySelect4Bits carryselect4bits_1 (
    .A(A[7:4]), .B(multiplexer_1_out_2), .C_In(fulladder_4_c_out), .C_Out(carryselect4bits_1_c_out),
    .S(S[7:4]));
  CarrySelect4Bits carryselect4bits_2 (
    .A(A[11:8]), .B(multiplexer_1_out_3), .C_In(carryselect4bits_1_c_out), .C_Out(carryselect4bits_2_c_out),
    .S(S[11:8]));
  CarrySelect4Bits carryselect4bits_3 (
    .A(A[15:12]), .B(multiplexer_1_out_4), .C_In(carryselect4bits_2_c_out), .C_Out(carryselect4bits_3_c_out),
    .S(S[15:12]));
  CarrySelect4Bits carryselect4bits_4 (
    .A(A[19:16]), .B(multiplexer_1_out_5), .C_In(carryselect4bits_3_c_out), .C_Out(carryselect4bits_4_c_out),
    .S(S[19:16]));
  CarrySelect4Bits carryselect4bits_5 (
    .A(A[23:20]), .B(multiplexer_1_out_6), .C_In(carryselect4bits_4_c_out), .C_Out(carryselect4bits_5_c_out),
    .S(S[23:20]));
  CarrySelect4Bits carryselect4bits_6 (
    .A(A[27:24]), .B(multiplexer_1_out_7), .C_In(carryselect4bits_5_c_out), .C_Out(carryselect4bits_6_c_out),
    .S(S[27:24]));
  CarrySelect4Bits carryselect4bits_7 (
    .A(A[31:28]), .B(multiplexer_1_out_8), .C_In(carryselect4bits_6_c_out), .S(S[31:28]));  // open: C_Out
endmodule
