// Digital circuit CarrySelect4Bits.dig as structural Verilog
module CarrySelect4Bits (
  input  [3:0] A,
  input  [3:0] B,
  input  C_In,
  output C_Out,
  output [3:0] S
);

  wire fulladder_1_c_out, fulladder_2_c_out, fulladder_3_c_out, fulladder_5_c_out, fulladder_6_c_out,
       fulladder_7_c_out;
  wire [4:0] fulladder_1_s, fulladder_8_c_out;

  FullAdder fulladder_1 (.A(A[0]), .B(B[0]), .C_In(1'b1), .S(fulladder_1_s[0]), .C_Out(fulladder_1_c_out));
  FullAdder fulladder_2 (.A(A[1]), .B(B[1]), .C_In(fulladder_1_c_out), .S(fulladder_1_s[1]), .C_Out(fulladder_2_c_out));
  FullAdder fulladder_3 (.A(A[2]), .B(B[2]), .C_In(fulladder_2_c_out), .S(fulladder_1_s[2]), .C_Out(fulladder_3_c_out));
  FullAdder fulladder_4 (.A(A[3]), .B(B[3]), .C_In(fulladder_3_c_out), .S(fulladder_1_s[3]), .C_Out(fulladder_1_s[4]));
  Multiplexer #(.Bits(5)) multiplexer_1 (.sel(C_In), .in_0(fulladder_8_c_out), .in_1(fulladder_1_s), .out({C_Out, S}));
  FullAdder fulladder_5 (.A(A[0]), .B(B[0]), .C_In(1'b0), .S(fulladder_8_c_out[0]), .C_Out(fulladder_5_c_out));
  FullAdder fulladder_6 (
    .A(A[1]), .B(B[1]), .C_In(fulladder_5_c_out), .S(fulladder_8_c_out[1]), .C_Out(fulladder_6_c_out));
  FullAdder fulladder_7 (
    .A(A[2]), .B(B[2]), .C_In(fulladder_6_c_out), .S(fulladder_8_c_out[2]), .C_Out(fulladder_7_c_out));
  FullAdder fulladder_8 (
    .A(A[3]), .B(B[3]), .C_In(fulladder_7_c_out), .S(fulladder_8_c_out[3]), .C_Out(fulladder_8_c_out[4]));
endmodule
