// Digital circuit Extensor com sinal.dig as structural Verilog
module Extensor_com_sinal (
  input  [15:0] In,
  output [23:0] Out
);

  Multiplexer #(.Bits(8)) multiplexer_1 (.sel(In[15]), .in_0({8{1'b0}}), .in_1({8{1'b1}}), .out(Out[23:16]));

  assign Out[15:0] = In;
endmodule
