// Digital circuit FullAdder.dig as structural Verilog
module FullAdder (
  input  A,
  input  B,
  input  C_In,
  output S,
  output C_Out
);

  wire and_1_out, and_2_out, xor_1_out;

  xor xor_1 (xor_1_out, A, B);
  xor xor_2 (S, xor_1_out, C_In);
  and and_1 (and_1_out, xor_1_out, C_In);
  and and_2 (and_2_out, B, A);
  or or_1 (C_Out, and_1_out, and_2_out);
endmodule
