// Digital circuit Instruction Pointer (IP).dig as structural Verilog
module Instruction_Pointer__IP (
  input  [23:0] Soma,
  input  clk,
  output [23:0] IP
);

  D_FF #(.Bits(24)) d_ff_1 (.D(Soma), .C(clk), .Q(IP));  // open: nQ
endmodule
