// Digital circuit Memória de Controle.dig as structural Verilog
module \Memória_de_Controle  (
  input  [3:0] Op,
  output W_E,
  output Sel_B,
  output [2:0] Sel_ULA,
  output E_Display,
  output Sel_Desvio,
  output Halt,
  output Branch
);

  ROM #(.AddrBits(4), .Bits(9)) rom_1 (
    .A(Op), .sel(1'b1), .D({Branch, Halt, Sel_ULA, Sel_Desvio, E_Display, Sel_B, W_E}));

  // Notes on the sheet:
  //   contents of rom_1 (hex, n*v repeats v):
  //   0,1,11,21,31,41,51,61,71,33,43,3,4,8,100,80
endmodule
