// Digital circuit Memória de Programa.dig as structural Verilog
module \Memória_de_Programa  (
  input  [23:0] IP,
  output [15:0] Const,
  output [3:0] c,
  output [3:0] b,
  output [3:0] Op,
  output [3:0] a
);

  ROM #(.AddrBits(24), .Bits(32)) rom_1 (.A(IP), .sel(1'b1), .D({Op, a, b, c, Const}));

  // Notes on the sheet:
  //   contents of rom_1 (hex, n*v repeats v):
  //   0,11210000,21340000,33450000,45460000,557a0000,660b0000,78bc0000
  //   ,89760000,9c0d5323,ac0e2aac,bd0702ad,c7000000,d0000001,e0000001,f0000000
endmodule
