// Digital circuit MicoX1.dig as structural Verilog
module MicoX1 (
  input  clk
);

  wire Branch, E_Display, Halt, Sel_B, Sel_Desvio, W_E, Zero;
  wire [2:0] Sel_ULA;
  wire [3:0] \memória_de_programa_1_a , \memória_de_programa_1_b , \memória_de_programa_1_c ,
       \memória_de_programa_1_op ;
  wire [15:0] \memória_de_programa_1_const ;
  wire [23:0] extensor_com_sinal_1_out, instruction_pointer__ip_1_ip, multiplexer_1_out, multiplexer_2_out,
       multiplexer_3_out, somador_1_s;
  wire [31:0] bancoderegistradores_1_a_2, bancoderegistradores_1_b_2, extensor_sem_sinal_1_out,
       multiplexer_4_out, multiplexer_5_out, ula_1_s;

  Multiplexer #(.Bits(24)) multiplexer_1 (
    .sel(Sel_Desvio), .in_0(24'h1), .in_1(extensor_com_sinal_1_out), .out(multiplexer_1_out));
  Multiplexer #(.Bits(24)) multiplexer_2 (
    .sel(Halt), .in_0(multiplexer_1_out), .in_1({24{1'b0}}), .out(multiplexer_2_out));
  Multiplexer #(.Bits(24)) multiplexer_3 (.sel(Zero), .in_0(multiplexer_2_out), .in_1(24'h1), .out(multiplexer_3_out));
  Instruction_Pointer__IP instruction_pointer__ip_1 (.Soma(somador_1_s), .clk(clk), .IP(instruction_pointer__ip_1_ip));
  Somador somador_1 (.A(instruction_pointer__ip_1_ip), .B(multiplexer_3_out), .S(somador_1_s));
  \Memória_de_Programa  \memória_de_programa_1  (
    .IP(instruction_pointer__ip_1_ip), .Const(\memória_de_programa_1_const ), .c(\memória_de_programa_1_c ),
    .b(\memória_de_programa_1_b ), .Op(\memória_de_programa_1_op ), .a(\memória_de_programa_1_a ));
  Extensor_com_sinal extensor_com_sinal_1 (.In(\memória_de_programa_1_const ), .Out(extensor_com_sinal_1_out));
  // Probe on \memória_de_programa_1_a 
  // Probe on \memória_de_programa_1_b 
  // Probe on \memória_de_programa_1_c 
  BancoDeRegistradores bancoderegistradores_1 (
    .a(\memória_de_programa_1_a ), .b(\memória_de_programa_1_b ), .c(\memória_de_programa_1_c ),
    .C_2(ula_1_s), .clk(clk), .W_E(W_E), .A_2(bancoderegistradores_1_a_2), .B_2(bancoderegistradores_1_b_2));
  Extensor_sem_sinal extensor_sem_sinal_1 (.In(\memória_de_programa_1_const ), .Out(extensor_sem_sinal_1_out));
  \Memória_de_Controle  \memória_de_controle_1  (
    .Op(\memória_de_programa_1_op ), .W_E(W_E), .Sel_B(Sel_B), .Sel_ULA(Sel_ULA), .E_Display(E_Display),
    .Sel_Desvio(Sel_Desvio), .Halt(Halt), .Branch(Branch));
  Multiplexer #(.Bits(32)) multiplexer_4 (
    .sel(Sel_B), .in_0(bancoderegistradores_1_b_2), .in_1(extensor_sem_sinal_1_out), .out(multiplexer_4_out));
  Multiplexer #(.Bits(32)) multiplexer_5 (
    .sel(E_Display), .in_0({32{1'b0}}), .in_1(bancoderegistradores_1_a_2), .out(multiplexer_5_out));
  ULA ula_1 (
    .A(bancoderegistradores_1_a_2), .B(multiplexer_4_out), .Op(Sel_ULA), .Branch(Branch), .S(ula_1_s),
    .Zero(Zero));
  // Probe on extensor_sem_sinal_1_out
  // Probe on multiplexer_5_out
endmodule
