// Digital circuit Somador.dig as structural Verilog
module Somador (
  input  [23:0] A,
  input  [23:0] B,
  output [23:0] S
);

  wire adder_1_c_out, adder_2_c_out, adder_3_c_out, adder_4_c_out, adder_5_c_out, adder_6_c_out,
       adder_7_c_out, adder_8_c_out, adder_9_c_out, adder_10_c_out, adder_11_c_out, adder_12_c_out,
       adder_13_c_out, adder_14_c_out, adder_15_c_out, adder_16_c_out, adder_17_c_out, adder_18_c_out,
       adder_19_c_out, adder_20_c_out, adder_21_c_out, adder_22_c_out, adder_23_c_out;

  Adder adder_1 (.A(A[0]), .B(B[0]), .S(S[0]), .C_Out(adder_1_c_out));
  Adder adder_2 (.A(A[1]), .B(adder_1_c_out), .S(S[1]), .C_Out(adder_2_c_out));
  Adder adder_3 (.A(A[2]), .B(adder_2_c_out), .S(S[2]), .C_Out(adder_3_c_out));
  Adder adder_4 (.A(A[3]), .B(adder_3_c_out), .S(S[3]), .C_Out(adder_4_c_out));
  Adder adder_5 (.A(A[4]), .B(adder_4_c_out), .S(S[4]), .C_Out(adder_5_c_out));
  Adder adder_6 (.A(A[5]), .B(adder_5_c_out), .S(S[5]), .C_Out(adder_6_c_out));
  Adder adder_7 (.A(A[6]), .B(adder_6_c_out), .S(S[6]), .C_Out(adder_7_c_out));
  Adder adder_8 (.A(A[7]), .B(adder_7_c_out), .S(S[7]), .C_Out(adder_8_c_out));
  Adder adder_9 (.A(A[8]), .B(adder_8_c_out), .S(S[8]), .C_Out(adder_9_c_out));
  Adder adder_10 (.A(A[9]), .B(adder_9_c_out), .S(S[9]), .C_Out(adder_10_c_out));
  Adder adder_11 (.A(A[10]), .B(adder_10_c_out), .S(S[10]), .C_Out(adder_11_c_out));
  Adder adder_12 (.A(A[11]), .B(adder_11_c_out), .S(S[11]), .C_Out(adder_12_c_out));
  Adder adder_13 (.A(A[12]), .B(adder_12_c_out), .S(S[12]), .C_Out(adder_13_c_out));
  Adder adder_14 (.A(A[13]), .B(adder_13_c_out), .S(S[13]), .C_Out(adder_14_c_out));
  Adder adder_15 (.A(A[14]), .B(adder_14_c_out), .S(S[14]), .C_Out(adder_15_c_out));
  Adder adder_16 (.A(A[15]), .B(adder_15_c_out), .S(S[15]), .C_Out(adder_16_c_out));
  Adder adder_17 (.A(A[16]), .B(adder_16_c_out), .S(S[16]), .C_Out(adder_17_c_out));
  Adder adder_18 (.A(A[17]), .B(adder_17_c_out), .S(S[17]), .C_Out(adder_18_c_out));
  Adder adder_19 (.A(A[18]), .B(adder_18_c_out), .S(S[18]), .C_Out(adder_19_c_out));
  Adder adder_20 (.A(A[19]), .B(adder_19_c_out), .S(S[19]), .C_Out(adder_20_c_out));
  Adder adder_21 (.A(A[20]), .B(adder_20_c_out), .S(S[20]), .C_Out(adder_21_c_out));
  Adder adder_22 (.A(A[21]), .B(adder_21_c_out), .S(S[21]), .C_Out(adder_22_c_out));
  Adder adder_23 (.A(A[22]), .B(adder_22_c_out), .S(S[22]), .C_Out(adder_23_c_out));
  Adder adder_24 (.A(A[23]), .B(adder_23_c_out), .S(S[23]));  // open: C_Out
endmodule
