// Digital circuit ULA.dig as structural Verilog
module ULA (
  input  [31:0] A,
  input  [31:0] B,
  input  [2:0] Op,
  input  Branch,
  output [31:0] S,
  output Zero
);

  wire [31:0] and_1_out, barrelshifter_1_out, barrelshifter_2_out, carryselect32bits_1_s, not_1_out,
       not_2_out, or_1_out, xor_1_out;

  CarrySelect32Bits carryselect32bits_1 (.A(A), .B(B), .\Subtração (Op), .S(carryselect32bits_1_s));
  assign and_1_out = A & B;  // And and_1, 32 bits wide
  assign or_1_out = A | B;  // Or or_1, 32 bits wide
  assign xor_1_out = A ^ B;  // XOr xor_1, 32 bits wide
  BarrelShifter #(.Bits(32)) barrelshifter_1 (.in(A), .shift(B[5:0]), .out(barrelshifter_1_out));
  BarrelShifter #(.Bits(32), .direction("right")) barrelshifter_2 (.in(A), .shift(B[5:0]), .out(barrelshifter_2_out));
  assign not_1_out = ~A;  // Not not_1, 32 bits wide
  Multiplexer #(.Selector_Bits(3), .Bits(32)) multiplexer_1 (
    .sel(Op), .in_0(carryselect32bits_1_s), .in_1(carryselect32bits_1_s), .in_2(and_1_out), .in_3(or_1_out),
    .in_4(xor_1_out), .in_5(not_1_out), .in_6(barrelshifter_1_out), .in_7(barrelshifter_2_out), .out(S));
  assign not_2_out = ~carryselect32bits_1_s;  // Not not_2, 32 bits wide
  and and_2 (Zero, Branch, not_2_out[0], not_2_out[1], not_2_out[2], not_2_out[3], not_2_out[4], not_2_out[5], not_2_out[6], not_2_out[7], not_2_out[8], not_2_out[9], not_2_out[10], not_2_out[11], not_2_out[12], not_2_out[13], not_2_out[14], not_2_out[15], not_2_out[16], not_2_out[17], not_2_out[18], not_2_out[19], not_2_out[20], not_2_out[21], not_2_out[22], not_2_out[23], not_2_out[24], not_2_out[25], not_2_out[26], not_2_out[27], not_2_out[28], not_2_out[29], not_2_out[30], not_2_out[31]);
endmodule
